# Fritzing sketch Detector de fuego (saved by Fritzing 1.0.6)

parts:
  A1 = 2 channel relay module [package=THT]
  BAT1 = 18650 battery holder [package=battery-18650-kit]
  A2 = j5019
  ARDUINO_NANO = Arduino Nano (Rev3.0) (ICSP)
  S1 = KY-026
  BOMBA = DC Motor [voltage_(max)=6V voltage_(min)=3V]
  BASE_DEL_MOTOR = Basic Servo
  SERVO_DE_MANGUERA = Basic Servo

nets:
  NO1: A1.pin_4, BOMBA.pin_1
  5V: A1.pin_5, A1.pin_13, A2.Pin_1, ARDUINO_NANO.5V, S1.pin3, BASE_DEL_MOTOR.vcc, SERVO_DE_MANGUERA.vcc
  GND: A1.pin_14, BAT1.+, A2.Pin_2, A2.Pin_5, ARDUINO_NANO.GND, S1.pin2, BOMBA.pin_2, BASE_DEL_MOTOR.gnd, SERVO_DE_MANGUERA.gnd
  IN1: A1.pin_15, ARDUINO_NANO.D11/MOSI
  BAT: BAT1.-, A2.Pin_6
  N1: ARDUINO_NANO.D8, S1.pin4
  D9: ARDUINO_NANO.D9, BASE_DEL_MOTOR.pulse
  D10: ARDUINO_NANO.D10, SERVO_DE_MANGUERA.pulse

custom parts:
  2 channel relay module: 2 channel Relay Module 5V 12V 24V High and Low Level Trigger Relay Control With Optocoupler Two Way relays DC 5 V 12 V 24 V Volt.
  18650 battery holder: 18650 Battery Holder identical to the dual battery version.
  j5019: This module is a small single cell lithium battery charging module which also includes a 1A step-up (boost) converter for powering a large range of applications.
  KY-026: ky-026 flame sensor module
