# Fritzing sketch Untitled Sketch (saved by Fritzing 1.0.6)

parts:
  BAT1 = 18650 battery holder [package=battery-18650-kit]
  BAT2 = 18650 battery holder [package=battery-18650-kit]
  Mod1 = 2S-BMS
  J1 = male pin header, 2 pins [form="♂ (male)"]
  M1 = RioRand LM2596
  SW1 = Slide_Switch_new
  M2 = DOIT Esp32 DevKit v1 (30 pins long, 11 pins width) [part_number=ESP32S-PIN30]
  J3 = Basic Servo
  J5 = Basic Servo
  J6 = Basic Servo
  J7 = Basic Servo
  J4 = Basic Servo
  J2 = Basic Servo
  S1 = Pushbutton [package="[THT]"]
  S2 = Pushbutton [package="[THT]"]
  S3 = Pushbutton [package="[THT]"]
  S4 = Pushbutton [package="[THT]"]
  S5 = Pushbutton [package="[THT]"]
  S6 = Pushbutton [package="[THT]"]
  S7 = Toggle Switch [package=THT]

nets:
  N1: BAT1.+, BAT2.-
  N2: BAT1.-, Mod1.pin1
  N3: BAT2.+, Mod1.pin2
  N4: Mod1.pin3#2, M1.Pin_2
  N5: Mod1.pin3#3, J1.pin1, SW1.pin_2
  N6: M1.Pin_1, SW1.pin_1
  N7: M1.Pin_4, M2.GND
  N8: M2.D4, S7.L1
  N9: M2.VP, S5.Pin_3, S5.Pin_4
  N10: M2.VN, S2.Pin_3, S2.Pin_4
  N11: M2.D34, S4.Pin_3, S4.Pin_4
  N12: M2.D35, S1.Pin_3, S1.Pin_4
  N13: M2.D32, S3.Pin_3, S3.Pin_4
  N14: M2.D33, S6.Pin_3, S6.Pin_4
  N15: M2.D25, J7.pulse
  N16: M2.D26, J6.pulse
  N17: M2.D27, J5.pulse
  N18: M2.D14, J4.pulse
  N19: M2.D12, J3.pulse
  N20: M2.D13, J2.pulse
  VIN: M2.VIN, J2.vcc

custom parts:
  18650 battery holder: 18650 Battery Holder identical to the dual battery version.
  2S-BMS: 2S-BMS LIPO battery charger / protection unit. Note pcb does not match the board as it will likely connect with wires, so pcb is 5 pads suitable for .1in header pins.
  Slide_Switch_new: the New two pin slide switch
  DOIT Esp32 DevKit v1 (30 pins long, 11 pins width): The DOIT Esp32 DevKit v1 is one of the development board created by DOIT to evaluate the ESP-WROOM-32 module. It is based on the ESP32 microcontroller that boasts Wifi, Bluetooth, Ethernet and Low Power support all in a single chip. (vanepp) made breadboard work, adjusted pin numbering and labels and reduced size of schematic and cleaned up pcb. This chip is 30pins long (2 x15) and 11 pins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
