# Fritzing sketch Untitled Sketch 4 (saved by Fritzing 1.0.6)

parts:
  Componente1 = Arduino Nano (Rev3.0)
  Componente2 = MQ-4
  Componente3 = LCD1602-I2C
  U1 = Mini-360 DC-DC Buck converter [package=THT]
  LED1 = LED - 5mm [color="Green (570nm)" current=0.030A package="5 mm [THT]"]
  LED2 = LED - 5mm [color="Yellow (595nm)" current=30mA package="5 mm [THT]"]
  LED3 = LED - 5mm [color="Red (633nm)" current=0.030A package="5 mm [THT]"]
  R1 = Resistor [tolerance=±5% power=0.25W resistance=220 package=THT]  # not connected
  R2 = Resistor [tolerance=±5% power=0.25W resistance=220 package=THT]  # not connected
  R3 = Resistor [tolerance=±5% power=0.25W resistance=220 package=THT]
  BAT1 = 18650 battery holder [package=battery-18650-kit]
  Mod1 = TP4056 [part_number=TP4056]
  SW1 = Slide_Switch_new
  J1 = Piezo Speaker  # not connected

nets:
  N1: Componente1.GND, U1.OUT+, R3.Pin_0
  N2: Componente1.D3, LED1.anode
  N3: Componente1.D4, LED2.anode
  N4: Componente1.D5, LED3.anode
  N5: Componente1.5V, U1.OUT-
  N6: Componente1.A5, Componente3.SCL
  N7: Componente1.A4, Componente3.SDA
  N8: Componente1.A0, Componente2.AO
  N9: U1.IN-, Mod1.pin6
  N10: U1.IN+, Mod1.pin3
  N11: BAT1.+, Mod1.pin5
  N12: Mod1.pin4, SW1.pin_2

custom parts:
  LCD1602-I2C: A standard character display, usually with 2x16 characters. Comes in many colors with LCM1602 IIC attached.
  Mini-360 DC-DC Buck converter: Mini-360 DC-DC Buck converter. Tiny buck step down voltage converter, input voltage 4.75 to 23V output 1 to 17V adjustable. Available from ebay and the like.
  18650 battery holder: 18650 Battery Holder identical to the dual battery version.
  TP4056: TP4056 Lithium battery charger / protection module. (this one has the pins on .1 boundaried unlike the original)
  Slide_Switch_new: the New two pin slide switch
