# Fritzing sketch Esquemático proyecto ascensor (saved by Fritzing 1.0.6)
breadboards: 1

parts:
  S1 = Pushbutton [package="[THT]"]
  S2 = Pushbutton [package="[THT]"]
  M1 = Getriebemotor  # not connected
  S3 = Toggle Switch dpdt [package=THT]
  JL012-13-5_1 = JL012-13-5.2 Lever (Limit) Switch SPDT + NO + NC [part_number=JL012-13-5.2]
  VCC1 = Battery block 9V [internal_resistance=0.1Ω]
  JL012-13-5_2 = JL012-13-5.2 Lever (Limit) Switch SPDT + NO + NC [part_number=JL012-13-5.2]

nets:
  N1: S1.Pin_1, S1.Pin_2, JL012-13-5_1.C
  N2: S1.Pin_3, S1.Pin_4, S2.Pin_3, S2.Pin_4, VCC1.+
  N3: S2.Pin_1, S2.Pin_2, JL012-13-5_2.C
  N4: S3.pin_1, JL012-13-5_1.NC
  N5: S3.pin_3, S3.pin_6, VCC1.-
  N6: S3.pin_4, JL012-13-5_2.NC

custom parts:
  Toggle Switch dpdt: Taiway Toggle Switch double pole double throw on-on-on. Breadboard copied from Steven Perry's Taiway 100-SP-X-T1 DPDT Miniature Toggle Switch part. Schematic is quite strange (because the switch is quite strange!) The toggle connects different pins together depending on its position. So connections are indicated by toggle position (hopefully clearly.)
  JL012-13-5.2 Lever (Limit) Switch SPDT + NO + NC: Micro Switch; Model No.: JL012-13.5-2; Actuator Action: Momentary; Actuator Type: Hinge Lever; Contact Configuration: 1NO, 1NC (SPDT) Temperature -25~65℃；Relative humidity: below 85%; Rate Voltage: 125V AC; Rated Current: 1A.
