# Fritzing sketch esquematico robot evasor de obstaculos (saved by Fritzing 1.0.6)

parts:
  Componente1 = Arduino Uno (Rev3) - ICSP
  Mod1 = TP4056 [part_number=TP4056]
  BAT1 = 18650 battery holder [package=battery-18650-kit]
  U1 = Mini-360 DC-DC Buck converter [package=THT]
  M1 = gear-motor  # not connected
  M2 = gear-motor  # not connected
  L298N1 = L298N DC motor driver
  HC-SR04_Sensor_1 = HC-SR04 Ultrasonic Distance Sensor

nets:
  N1: Componente1.D8, HC-SR04_Sensor_1.ECHO
  N2: Componente1.D9_PWM, HC-SR04_Sensor_1.TRIG
  N3: Componente1.D4, L298N1.IN1
  N4: Componente1.D5_PWM, L298N1.IN2
  N5: Componente1.D6_PWM, L298N1.IN3
  N6: Componente1.D7, L298N1.IN4
  N7: Componente1.5V, U1.OUT+
  N8: Componente1.GND, U1.OUT-
  N9: Mod1.pin3, U1.IN+
  N10: Mod1.pin4, BAT1.-
  N11: Mod1.pin5, BAT1.+
  N12: Mod1.pin6, U1.IN-
  N13: L298N1.5V#9, L298N1.ENA
  N14: L298N1.5V#10, L298N1.ENB

custom parts:
  TP4056: TP4056 Lithium battery charger / protection module. (this one has the pins on .1 boundaried unlike the original)
  18650 battery holder: 18650 Battery Holder identical to the dual battery version.
  Mini-360 DC-DC Buck converter: Mini-360 DC-DC Buck converter. Tiny buck step down voltage converter, input voltage 4.75 to 23V output 1 to 17V adjustable. Available from ebay and the like.
  L298N DC motor driver: 2x DC motor driver with 78M05 positive voltage regulator (7..35 V) L298N: max 46 V, 2 A Set 5 V Enable jumper to enable 5 V regultor (needed for the L298N) and +5 V output at screw terminal or supply external +5 V at screw terminal Set ENA and/or ENB to +5 V to enable motor permanently or supply ENA and/or ENB with PWM signal IN1 and IN2 set rotation directory for motor A (OUT1/OUT2) IN2 and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
