# Fritzing sketch Esquematico Noria Fritzing (saved by Fritzing 1.0.6)

parts:
  Componente1 = Arduino Nano (Rev3.0) (ICSP)
  MOTOR1 = 28BYJ-48 Stepper Motor
  BREAKOUT1 = ULN2003A breakout board
  R2 = Rotary Potentiometer (Large) [maximum_resistance=10kΩ knob_status=50% power=0.5W package=THT]
  Power_plug1 = Power plug
  SW1 = Slide_Switch_new

nets:
  GND: Componente1.GND, Power_plug1.GND
  N1: Componente1.D8, BREAKOUT1.In_1
  N2: Componente1.D9, BREAKOUT1.In_2
  N3: Componente1.D10, BREAKOUT1.In_3
  N4: Componente1.D11/MOSI, BREAKOUT1.In_4
  N5: Componente1.A0, R2.wiper
  N6: MOTOR1.BLUE, BREAKOUT1.BLUE_wire
  N7: MOTOR1.PINK, BREAKOUT1.PINK_wire
  N8: MOTOR1.RED, BREAKOUT1.RED_wire
  N9: MOTOR1.ORANGE, BREAKOUT1.ORANGE_wire
  N10: MOTOR1.YELLOW, BREAKOUT1.YELLOW_wire
  N11: Power_plug1.VCC, SW1.pin_1

custom parts:
  28BYJ-48 Stepper Motor: 28BYJ-48 gear-reduction stepper motor (small)
  ULN2003A breakout board: ULN2003A 7-way Darlington Transistor Driver on breakoutboard
  Slide_Switch_new: the New two pin slide switch
