# Fritzing sketch Esquematico Proyecno no vidente (saved by Fritzing 1.0.6)

parts:
  M1 = DOIT Esp32 DevKit v1 (30 pins long, 11 pins width) [part_number=ESP32S-PIN30]
  BAT1 = 18650 battery holder [package=battery-18650-kit]
  A1 = j5019
  HC-SR04_Sensor_1 = HC-SR04 Ultrasonic Distance Sensor

nets:
  N1: M1.D5, HC-SR04_Sensor_1.TRIG
  GND: M1.GND, BAT1.+, A1.Pin_2, A1.Pin_5, HC-SR04_Sensor_1.GND
  5V: M1.VIN, A1.Pin_1, HC-SR04_Sensor_1.VCC
  BAT: BAT1.-, A1.Pin_6
  ECHO: HC-SR04_Sensor_1.ECHO

custom parts:
  DOIT Esp32 DevKit v1 (30 pins long, 11 pins width): The DOIT Esp32 DevKit v1 is one of the development board created by DOIT to evaluate the ESP-WROOM-32 module. It is based on the ESP32 microcontroller that boasts Wifi, Bluetooth, Ethernet and Low Power support all in a single chip. (vanepp) made breadboard work, adjusted pin numbering and labels and reduced size of schematic and cleaned up pcb. This chip is 30pins long (2 x15) and 11 pins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
  18650 battery holder: 18650 Battery Holder identical to the dual battery version.
  j5019: This module is a small single cell lithium battery charging module which also includes a 1A step-up (boost) converter for powering a large range of applications.
