# Fritzing sketch Esquematico Proyecno no vidente V2 (saved by Fritzing 1.0.6)
circuit board: 11.573cm x 7.96812cm

parts:
  ESP32DEVKIT = DOIT Esp32 DevKit v1 (30 pins long, 11 pins width) [part_number=ESP32S-PIN30]
  J5019 = j5019
  MOTOR_VIBRADOR_3V = DC Motor [voltage_(max)=3.3V voltage_(min)=3V]
  BUZZER = Piezo Speaker
  SOS = Round Pushbutton
  Parlante_8_Ω_/_1_W = Loudspeaker
  R3 = Resistor [tolerance=±5% power=0.25W resistance=1k package=THT]
  R4 = Resistor [tolerance=±5% power=0.25W resistance=100k package=THT]
  C3 = Electrolytic Capacitor [capacitance=1000μF voltage=16V package="100 mil [THT, electrolytic]"]
  C5 = Electrolytic Capacitor [capacitance=470µF voltage=16V package="100 mil [THT, electrolytic]"]
  C2 = Electrolytic Capacitor [capacitance=470µF voltage=10V package="100 mil [THT, electrolytic]"]
  C1 = Electrolytic Capacitor [capacitance=1000μF voltage=16V package="100 mil [THT, electrolytic]"]
  D1 = Rectifier Diode [part_number=1N4007 package="300 mil [THT]"]
  D2 = Rectifier Diode [part_number=1N4007 package="300 mil [THT]"]
  D3 = Rectifier Diode [part_number=1N4007 package="300 mil [THT]"]
  Q2 = NPN-Transistor [part_number=2n2222 package="TO92 [THT]"]
  BATERÍA = Screw terminal - 2 pins [package=THT]
  GPS_NEO-6M = male pin header, 5 pins [form="♂ (male)"]
  HC-SR04 = male pin header, 4 pins [form="♂ (male)"]
  R5 = Resistor [tolerance=±5% power=0.25W resistance=2k package=THT]
  R6 = Resistor [tolerance=±5% power=0.25W resistance=1k package=THT]
  SIM800L_BO1 = SIM800L BO
  C9 = Ceramic Capacitor [capacitance=100nF voltage=50V package="100 mil [THT, multilayer]"]
  C10 = Ceramic Capacitor [capacitance=100nF voltage=50V package="100 mil [THT, multilayer]"]
  C11 = Ceramic Capacitor [capacitance=100nF voltage=50V package="100 mil [THT, multilayer]"]
  C12 = Ceramic Capacitor [capacitance=100nF voltage=50V package="100 mil [THT, multilayer]"]
  ESP32-CAM = ESP32 - CAM
  C13 = Ceramic Capacitor [capacitance=100nF voltage=50V package="100 mil [THT, multilayer]"]
  C14 = Electrolytic Capacitor [capacitance=470µF voltage=16V package="100 mil [THT, electrolytic]"]

nets:
  GND: ESP32DEVKIT.GND, J5019.Pin_2, J5019.Pin_4, J5019.Pin_5, BUZZER.pin1, SOS.leg0, Parlante_8_Ω_/_1_W.pin2, R4.Pin_0, C3.-, C5.-, C1.-, Q2.E, BATERÍA.pin1, GPS_NEO-6M.pin4, HC-SR04.pin4, R6.Pin_0, SIM800L_BO1.pin_6, C9.0, C10.0, C11.0, C12.0, ESP32-CAM.GND, C13.0, C14.-
  TXD: ESP32DEVKIT.D4, GPS_NEO-6M.pin3
  GPIO 16: ESP32DEVKIT.RX2, SIM800L_BO1.pin_5
  GPIO 17: ESP32DEVKIT.TX2, SIM800L_BO1.pin_4
  TRIG: ESP32DEVKIT.D5, HC-SR04.pin2
  ECHO: ESP32DEVKIT.D18, R5.Pin_0
  GPIO 22: ESP32DEVKIT.D22, ESP32-CAM.VOT
  GPIO 23: ESP32DEVKIT.D23, ESP32-CAM.VOR
  GPIO 32: ESP32DEVKIT.D32, R3.Pin_0
  GPIO 25: ESP32DEVKIT.D25, C2.+
  GPIO 27: ESP32DEVKIT.D27, SOS.leg1
  RXD: ESP32DEVKIT.D14, GPS_NEO-6M.pin2
  GPIO 13: ESP32DEVKIT.D13, BUZZER.pin2
  5V: ESP32DEVKIT.VIN, J5019.Pin_1, MOTOR_VIBRADOR_3V.pin_1, C3.+, C5.+, C1.+, D2.anode, D3.cathode, GPS_NEO-6M.pin5, HC-SR04.pin1, C9.1, C10.1, C11.1, C12.1, ESP32-CAM.5V, C13.1, C14.+
  BAT: J5019.Pin_6, BATERÍA.pin2
  N1: MOTOR_VIBRADOR_3V.pin_2, D3.anode, Q2.C
  N2: Parlante_8_Ω_/_1_W.pin1, C2.-
  N3: R3.Pin_1, R4.Pin_1, Q2.B
  N4: D1.cathode, SIM800L_BO1.PIN2
  N5: D1.anode, D2.cathode
  N6: HC-SR04.pin3, R5.Pin_1, R6.Pin_1

notes:
  VCC
  GND
  TXD
  RXD
  ECHO
  TRIG
  +
  -
  AJTecnology.com

custom parts:
  DOIT Esp32 DevKit v1 (30 pins long, 11 pins width): The DOIT Esp32 DevKit v1 is one of the development board created by DOIT to evaluate the ESP-WROOM-32 module. It is based on the ESP32 microcontroller that boasts Wifi, Bluetooth, Ethernet and Low Power support all in a single chip. (vanepp) made breadboard work, adjusted pin numbering and labels and reduced size of schematic and cleaned up pcb. This chip is 30pins long (2 x15) and 11 pins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
  j5019: This module is a small single cell lithium battery charging module which also includes a 1A step-up (boost) converter for powering a large range of applications.
  ESP32 - CAM: The ESP32-CAM has a very competitive small-size camera module that can operate independently as a minimum system with a footprint of only 27*40.5*4.5mm and a deep sleep current of up to 6mA.
